# Fritzing sketch AirQ (saved by Fritzing 0.9.4)
circuit board: 4.67811cm x 3.37928cm

parts:
  Q1 = NPN-Transistor [package="TO92 [THT]"]
  Q2 = NPN-Transistor [package="TO92 [THT]"]
  Q3 = NPN-Transistor [package="TO92 [THT]"]
  C1 = Electrolytic Capacitor [capacitance=1µF package="100 mil [THT, electrolytic]"]
  YELLOW = Super Flux LED blue [color=Yellow]
  GREEN = Super Flux LED blue [color=Green]
  RED = Super Flux LED blue [color=Red]
  J1 = Piezo Speaker
  R1 = Resistor [tolerance=±5% resistance=100 package="2010 [SMD]"]
  R2 = Resistor [tolerance=±5% resistance=100 package="2010 [SMD]"]
  R3 = Resistor [tolerance=±5% resistance=100 package="2010 [SMD]"]
  U1 = Mini-USB _B_ connector with 5th pin broken out. [package=usb-minib]
  J2 = female pin header, 5 pins [form="♀ (female)"]
  R4 = Trimmer Potentiometer [maximum_resistance=10kΩ package=THT]
  Arduino_ProMini = Arduino Pro Mini (3.3V)
  LCD1 = LCD screen
  J3 = female pin header, 2 pins [form="♀ (female)"]

nets:
  GND: Q1.E, Q2.E, Q3.E, C1.-, J1.pin1, U1.MTN2, U1.MTN3, U1.MTN1, U1.MTN4, U1.GND, J2.pin2, J2.pin5, R4.leg1, Arduino_ProMini.GND, LCD1.VSS, LCD1.R/W, LCD1.LED-, J3.pin1
  N1: Q1.B, Arduino_ProMini.D10
  N2: Q1.C, RED.cathode
  N3: Q2.B, Arduino_ProMini.MOSI
  N4: Q2.C, YELLOW.cathode
  N5: Q3.B, Arduino_ProMini.MISO
  N6: Q3.C, GREEN.cathode
  N7: C1.+, J2.pin1, R4.leg2, Arduino_ProMini.VCC, J3.pin2
  N8: YELLOW.anode, R2.Pin_0
  N9: GREEN.anode, R1.Pin_0
  N10: RED.anode, R3.Pin_0
  N11: J1.pin2, Arduino_ProMini.SCK
  N12: R1.Pin_1, R2.Pin_1, R3.Pin_1, U1.VBUS, Arduino_ProMini.RAW, LCD1.VDD
  N13: J2.pin3, Arduino_ProMini.A5
  N14: J2.pin4, Arduino_ProMini.A4
  N15: R4.wiper, LCD1.V0
  N16: Arduino_ProMini.D9, LCD1.LED+
  N17: Arduino_ProMini.D8, LCD1.DB7
  N18: Arduino_ProMini.D7, LCD1.DB6
  N19: Arduino_ProMini.D6, LCD1.DB5
  N20: Arduino_ProMini.D5, LCD1.DB4
  N21: Arduino_ProMini.D3, LCD1.E
  N22: Arduino_ProMini.D2, LCD1.RS

notes:
  3.3V Edition
